# Fritzing sketch Project_Circuit (saved by Fritzing 0.8.7b)
stripboards: 1

parts:
  U1 = NodeMCU V3.0
  Sensor1 = Gas Sensor Breakout Board
  Load_Cell1 = Load Cell - Red/white/black/green
  Part1 = HX711 Weighing Sensor Module
  SG1 = Buzzer 12mm [package=buzzer-12mm]
  R1 = Resistor [tolerance=±5% resistance=220 package=THT]
  U3 = LCD-16X2 [package=lcd-16x2]
  LCM1602_IIC1 = LCM1602 IIC [part_number="LCM1602 IIC" chip_label="LCM1602 IIC" package="DIP (Dual Inline) [THT]"]
  R2 = Resistor [tolerance=±5% resistance=220 package=THT]
  Mod1 = generic-ac-power-supply [package=THT]

nets:
  N1: U1.D1, LCM1602_IIC1.SCL
  N2: U1.D2, LCM1602_IIC1.SDA
  GND: U1.GND, Sensor1.GND, Part1.GND, SG1.1, LCM1602_IIC1.GND, R2.Pin_1, Mod1.pin4
  N3: U1.D5, Part1.DO/RX
  N4: U1.D6, Part1.CK/TX
  N5: U1.D7, SG1.2
  VIN: U1.Vin, Sensor1.5V, Part1.VCC, R1.Pin_0, R2.Pin_0
  N6: U1.A0, Sensor1.AOUT
  N7: Load_Cell1.wire1, Part1.E+
  N8: Load_Cell1.wire2, Part1.A+
  N9: Load_Cell1.wire3, Part1.E-
  N10: Load_Cell1.wire4, Part1.A-
  N11: R1.Pin_1, Mod1.pin3
  VSS: U3.VSS, LCM1602_IIC1.VSS
  VDD: U3.VDD, LCM1602_IIC1.VDD
  N12: U3.VO, LCM1602_IIC1.V0
  N13: U3.RS, LCM1602_IIC1.RS
  N14: U3.R_W, LCM1602_IIC1.RW
  N15: U3.E, LCM1602_IIC1.E
  N16: U3.DB0, LCM1602_IIC1.D0
  N17: U3.DB1, LCM1602_IIC1.D1
  N18: U3.DB2, LCM1602_IIC1.D2
  N19: U3.DB3, LCM1602_IIC1.D3
  N20: U3.DB4, LCM1602_IIC1.D4
  N21: U3.DB5, LCM1602_IIC1.D5
  N22: U3.DB6, LCM1602_IIC1.D6
  N23: U3.DB7, LCM1602_IIC1.D7
  N24: U3.A, LCM1602_IIC1.A
  N25: U3.K, LCM1602_IIC1.K

custom parts:
  NodeMCU V3.0: ESP8266 based NodeMCU
  Gas Sensor Breakout Board: Gas sensor breakout board. Input voltage is 5V. Sensor output is available in analog and digital.
  Load Cell - Red/white/black/green: A rectangle load cell/weighting pressure Sensor with four wires - Red, white, black, green. Normally corresponding with E+, E-, A+, A- respectively.
  HX711 Weighing Sensor Module: HX711 is a precision 24-bit analog-to-digital converter (ADC) designed for weigh scales and industrial control applications to interface directly with a bridge sensor.
  LCM1602 IIC: I2C-Module to use a 1602 or 2004 LCD on with the wire.h libory Serial LCD Modul
  generic-ac-power-supply: Generic ac power supply module. Use as is, or customize the svgs to fit your particular device (as they are all different.) Provides AC input and single DC output. This is variant 2, with pcb modified to match the url for a specific device.
